// Logisim project Elektroquemon.circ as structural Verilog: 1 circuit, main circuit Juego Elektroquemón
module \Juego_Elektroquemón  (
  input  Avanzado,
  input  Intermedio,
  input  Basico,
  output J1,
  output B,
  output K1,
  output Q1,
  output Q0,
  output J0,
  output _4,
  output Valor_A,
  output J2,
  output K2,
  output _3,
  output J1_2,
  output _2,
  output _0,
  output K1_2,
  output J0_2,
  output K0
);

  wire and_1_out, and_2_out, and_3_out, and_4_out, and_5_out, and_7_out, and_8_out, and_9_out, and_10_out,
       and_11_out, and_12_out, and_13_out, and_14_out, and_15_out, and_16_out, and_17_out, and_18_out,
       and_19_out, and_20_out, and_21_out, and_22_out, and_23_out, and_24_out, and_25_out, and_26_out,
       and_27_out, and_28_out, and_29_out, and_30_out, and_31_out, and_32_out, and_33_out, and_34_out,
       and_35_out, and_36_out, and_37_out, and_38_out, and_39_out, button_1_out, clock_1_out,
       comparator_1_eq, comparator_1_gt, comparator_2_eq, comparator_2_gt, comparator_3_gt, comparator_4_gt,
       comparator_5_gt, comparator_6_eq, controlled_buffer_1_out, controlled_buffer_4_out,
       controlled_buffer_5_out, controlled_buffer_6_out, controlled_buffer_7_out, d_ff_1_q, d_ff_1_qn,
       d_ff_2_q, d_ff_2_qn, d_ff_3_q, d_ff_3_qn, d_ff_4_q, j_k_ff_1_qn, j_k_ff_5_qn, j_k_ff_6_qn, not_1_out,
       not_2_out, not_3_out, not_4_out, not_5_out, not_6_out, not_7_out, not_8_out, not_9_out, not_10_out,
       not_11_out, not_12_out, not_13_out, not_14_out, not_15_out, not_16_out, not_17_out, not_18_out,
       not_19_out, not_20_out, not_21_out, or_1_out, or_2_out, or_4_out, or_10_out, or_13_out, t_ff_2_q,
       xor_1_out;
  wire [2:0] j_k_ff_4_q;
  wire [3:0] j_k_ff_1_q, multiplexer_1_out, multiplexer_2_out, multiplexer_3_out, multiplexer_4_out,
       multiplexer_5_out, subtractor_1_out, subtractor_2_out, subtractor_3_out;

  Clock clock_1 (.out(clock_1_out));
  or or_1 (or_1_out, Avanzado, Intermedio, Basico);
  D_Flip_Flop d_ff_1 (.clk(clock_1_out), .D(d_ff_1_qn), .Q(d_ff_1_q), .Qn(d_ff_1_qn));  // open: preset, en, reset
  D_Flip_Flop d_ff_2 (.clk(clock_1_out), .D(d_ff_2_qn), .Q(d_ff_2_q), .Qn(d_ff_2_qn));  // open: preset, en, reset
  or or_2 (or_2_out, and_4_out, and_5_out);
  or or_3 (Valor_A, and_20_out, controlled_buffer_7_out);
  and and_1 (and_1_out, ~Avanzado, Intermedio);  // AND_Gate
  and and_2 (and_2_out, ~Avanzado, ~Intermedio, Basico);  // AND_Gate
  D_Flip_Flop d_ff_3 (.clk(d_ff_2_q), .D(d_ff_3_qn), .Q(d_ff_3_q), .Qn(d_ff_3_qn));  // open: preset, en, reset
  not not_1 (not_1_out, Valor_A);
  not not_2 (not_2_out, j_k_ff_4_q[1]);
  not not_3 (not_3_out, Valor_A);
  not not_4 (not_4_out, Valor_A);
  not not_5 (not_5_out, j_k_ff_4_q[0]);
  not not_6 (not_6_out, j_k_ff_4_q[2]);
  not not_7 (not_7_out, j_k_ff_4_q[1]);
  not not_8 (not_8_out, Valor_A);
  not not_9 (not_9_out, j_k_ff_4_q[2]);
  LED \Ganó  (.in(and_31_out));
  Hex_Digit_Display hex_digit_display_1 (.value(multiplexer_3_out));  // open: dp
  T_Flip_Flop t_ff_1 (
    .clk(controlled_buffer_5_out), .Q(B), .preset(controlled_buffer_5_out));  // open: T, Qn, reset, en
  or or_4 (or_4_out, controlled_buffer_5_out, and_20_out, and_3_out);
  and and_3 (and_3_out, clock_1_out, and_17_out);
  assign controlled_buffer_1_out = Avanzado ? clock_1_out : 1'bz;  // Controlled_Buffer controlled_buffer_1
  assign controlled_buffer_1_out = and_1_out ? d_ff_1_q : 1'bz;  // Controlled_Buffer controlled_buffer_2
  assign controlled_buffer_1_out = and_2_out ? d_ff_3_q : 1'bz;  // Controlled_Buffer controlled_buffer_3
  and and_4 (and_4_out, ~Q0, ~Q1);  // AND_Gate
  and and_5 (and_5_out, and_17_out, and_21_out);
  and and_6 (J2, not_1_out, j_k_ff_4_q[1], j_k_ff_4_q[0]);
  and and_7 (and_7_out, j_k_ff_4_q[1], j_k_ff_4_q[0]);
  and and_8 (and_8_out, Valor_A, not_2_out);
  and and_9 (and_9_out, not_3_out, j_k_ff_4_q[0]);
  and and_10 (and_10_out, Valor_A, j_k_ff_4_q[2]);
  and and_11 (and_11_out, not_4_out, j_k_ff_4_q[0]);
  and and_12 (and_12_out, Valor_A, not_5_out);
  and and_13 (and_13_out, Valor_A, j_k_ff_4_q[2]);
  not not_10 (not_10_out, Valor_A);
  and and_14 (and_14_out, not_6_out, j_k_ff_4_q[1]);
  and and_15 (and_15_out, j_k_ff_4_q[2], not_7_out);
  or or_5 (K0, not_8_out, not_9_out, j_k_ff_4_q[1]);
  LED \Perdió  (.in(and_30_out));
  Hex_Digit_Display hex_digit_display_2 (.value(multiplexer_2_out));  // open: dp
  Button button_1 (.out(button_1_out));
  and and_16 (and_16_out, ~Q0, Q1);  // AND_Gate
  assign controlled_buffer_4_out = and_16_out ? controlled_buffer_1_out : 1'bz;  // Controlled_Buffer controlled_buffer_4
  and and_17 (and_17_out, Q0, ~Q1);  // AND_Gate
  or or_6 (K2, and_7_out, and_8_out);
  or or_7 (J1_2, and_9_out, and_10_out);
  or or_8 (K1_2, and_11_out, and_12_out, and_13_out);
  or or_9 (J0_2, not_10_out, and_14_out, and_15_out);
  assign controlled_buffer_5_out = or_1_out ? and_34_out : 1'bz;  // Controlled_Buffer controlled_buffer_5
  not not_11 (not_11_out, B);
  not not_12 (not_12_out, B);
  not not_13 (not_13_out, Q1);
  J_K_Flip_Flop j_k_ff_1 (
    .J(1'b1), .clk(controlled_buffer_4_out), .K(1'b1), .Q(j_k_ff_1_q[0]), .Qn(j_k_ff_1_qn), .preset(or_10_out));  // open: en, reset
  or or_10 (or_10_out, and_17_out, and_20_out);
  J_K_Flip_Flop j_k_ff_2 (.J(J2), .clk(or_2_out), .K(K2), .Q(j_k_ff_4_q[2]));  // open: Qn, preset, en, reset
  J_K_Flip_Flop j_k_ff_3 (.J(J1_2), .clk(or_2_out), .K(K1_2), .Q(j_k_ff_4_q[1]));  // open: Qn, preset, en, reset
  J_K_Flip_Flop j_k_ff_4 (.J(J0_2), .clk(or_2_out), .K(K0), .Q(j_k_ff_4_q[0]));  // open: Qn, preset, en, reset
  or or_11 (J1, not_11_out, Q0);
  and and_18 (and_18_out, not_12_out, Q1);
  and and_19 (and_19_out, B, not_13_out);
  and and_20 (and_20_out, j_k_ff_1_q[0], j_k_ff_5_qn, j_k_ff_1_q[2], j_k_ff_1_q[3]);
  and and_21 (and_21_out, j_k_ff_4_q[2], j_k_ff_4_q[1], j_k_ff_4_q[0]);
  LED Colobo (.in(and_22_out));
  and and_22 (and_22_out, j_k_ff_4_q[2], j_k_ff_4_q[1], j_k_ff_4_q[0]);
  and and_23 (and_23_out, j_k_ff_4_q[2], j_k_ff_4_q[1], ~j_k_ff_4_q[0]);  // AND_Gate
  LED \Lémur  (.in(and_23_out));
  and and_24 (and_24_out, j_k_ff_4_q[2], ~j_k_ff_4_q[1], j_k_ff_4_q[0]);  // AND_Gate
  LED Perro_Gato (.in(and_24_out));
  LED Raton (.in(and_25_out));
  and and_25 (and_25_out, j_k_ff_4_q[2], ~j_k_ff_4_q[1], ~j_k_ff_4_q[0]);  // AND_Gate
  LED Lagarto (.in(and_26_out));
  and and_26 (and_26_out, ~j_k_ff_4_q[2], j_k_ff_4_q[1], j_k_ff_4_q[0]);  // AND_Gate
  and and_27 (and_27_out, ~j_k_ff_4_q[2], j_k_ff_4_q[1], ~j_k_ff_4_q[0]);  // AND_Gate
  LED \Camarón  (.in(and_27_out));
  and and_28 (and_28_out, ~j_k_ff_4_q[2], ~j_k_ff_4_q[1], j_k_ff_4_q[0]);  // AND_Gate
  LED Caracol (.in(and_28_out));
  LED Amiba (.in(and_29_out));
  and and_29 (and_29_out, ~j_k_ff_4_q[2], ~j_k_ff_4_q[1], ~j_k_ff_4_q[0]);  // AND_Gate
  or or_12 (J0, and_18_out, and_19_out);
  J_K_Flip_Flop j_k_ff_5 (
    .J(1'b1), .clk(j_k_ff_1_qn), .K(1'b1), .Q(j_k_ff_1_q[1]), .Qn(j_k_ff_5_qn), .preset(or_10_out),
    .reset(or_10_out));  // open: en
  J_K_Flip_Flop u_Q1 (.J(J1), .clk(or_4_out), .K(1'b1), .Q(Q1));  // open: Qn, preset, en, reset
  J_K_Flip_Flop u_Q0 (.J(J0), .clk(or_4_out), .K(1'b1), .Q(Q0));  // open: Qn, preset, en, reset
  J_K_Flip_Flop j_k_ff_6 (
    .J(1'b1), .clk(j_k_ff_5_qn), .K(1'b1), .Q(j_k_ff_1_q[2]), .Qn(j_k_ff_6_qn), .preset(or_10_out),
    .reset(or_10_out));  // open: en
  and and_30 (and_30_out, controlled_buffer_6_out, ~j_k_ff_4_q[2], ~j_k_ff_4_q[1], ~j_k_ff_4_q[0]);  // AND_Gate
  and and_31 (and_31_out, and_32_out, and_33_out);
  and and_32 (and_32_out, j_k_ff_4_q[2], j_k_ff_4_q[1], j_k_ff_4_q[0]);
  D_Flip_Flop d_ff_4 (.clk(clock_1_out), .D(button_1_out), .Q(d_ff_4_q));  // open: Qn, preset, en, reset
  and and_33 (and_33_out, ~Q1, ~Q0);  // AND_Gate
  J_K_Flip_Flop j_k_ff_7 (
    .J(1'b1), .clk(j_k_ff_6_qn), .K(1'b1), .Q(j_k_ff_1_q[3]), .preset(or_10_out), .reset(or_10_out));  // open: Qn, en
  xor xor_1 (xor_1_out, d_ff_4_q, button_1_out);
  and and_34 (and_34_out, xor_1_out, button_1_out);
  and and_35 (and_35_out, ~Q1, ~Q0);  // AND_Gate
  Multiplexer #(.width(4), .enable("false")) multiplexer_1 (
    .in0(4'b0111), .in1(j_k_ff_1_q), .out(multiplexer_1_out), .sel(t_ff_2_q));
  T_Flip_Flop t_ff_2 (
    .clk(controlled_buffer_5_out), .Q(t_ff_2_q), .preset(controlled_buffer_5_out));  // open: T, Qn, reset, en
  Subtractor #(.width(4)) subtractor_1 (.a(j_k_ff_1_q), .b(4'b1010), .out(subtractor_1_out));  // open: bin, bout
  Multiplexer #(.width(4), .enable("false")) multiplexer_2 (
    .in0(j_k_ff_1_q), .in1(subtractor_1_out), .out(multiplexer_2_out), .sel(or_13_out));
  Comparator #(.width(4), .mode("unsigned")) comparator_1 (
    .a(j_k_ff_1_q), .b(4'b1010), .gt(comparator_1_gt), .eq(comparator_1_eq));  // open: lt
  or or_13 (or_13_out, comparator_1_eq, comparator_1_gt);
  Multiplexer #(.width(4), .enable("false")) multiplexer_3 (
    .in0(4'b0000), .in1(4'b0001), .out(multiplexer_3_out), .sel(or_13_out));
  assign controlled_buffer_6_out = and_35_out ? controlled_buffer_7_out : 1'bz;  // Controlled_Buffer controlled_buffer_6
  Subtractor #(.width(4)) subtractor_2 (.a(4'b0111), .b(multiplexer_1_out), .out(subtractor_2_out));  // open: bin, bout
  Subtractor #(.width(4)) subtractor_3 (.a(multiplexer_1_out), .b(4'b0111), .out(subtractor_3_out));  // open: bin, bout
  Comparator #(.width(4), .mode("unsigned")) comparator_2 (
    .a(multiplexer_1_out), .b(4'b0111), .gt(comparator_2_gt), .eq(comparator_2_eq));  // open: lt
  not not_14 (not_14_out, j_k_ff_4_q[2]);
  not not_15 (not_15_out, j_k_ff_4_q[1]);
  not not_16 (not_16_out, j_k_ff_4_q[2]);
  not not_17 (not_17_out, j_k_ff_4_q[1]);
  not not_18 (not_18_out, j_k_ff_4_q[0]);
  not not_19 (not_19_out, j_k_ff_4_q[1]);
  not not_20 (not_20_out, j_k_ff_4_q[0]);
  Multiplexer #(.width(4), .enable("false")) multiplexer_4 (
    .in0(subtractor_2_out), .in1(subtractor_3_out), .out(multiplexer_4_out), .sel(comparator_2_gt));
  Multiplexer #(.width(4), .enable("false")) multiplexer_5 (
    .in0(multiplexer_4_out), .in1(4'b0000), .out(multiplexer_5_out), .sel(comparator_2_eq));
  and and_36 (and_36_out, not_14_out, not_15_out);
  and and_37 (and_37_out, j_k_ff_4_q[2], j_k_ff_4_q[1], j_k_ff_4_q[0]);
  and and_38 (and_38_out, not_16_out, j_k_ff_4_q[1]);
  and and_39 (and_39_out, j_k_ff_4_q[2], not_17_out, not_18_out);
  and and_40 (_2, j_k_ff_4_q[2], not_19_out, j_k_ff_4_q[0]);
  and and_41 (_0, j_k_ff_4_q[2], j_k_ff_4_q[1], not_20_out);
  Hex_Digit_Display hex_digit_display_3 (.value(multiplexer_5_out));  // open: dp
  or or_14 (_4, and_36_out, and_37_out);
  or or_15 (_3, and_38_out, and_39_out);
  Comparator #(.width(4), .mode("unsigned")) comparator_3 (
    .a(multiplexer_5_out), .b(4'b0100), .gt(comparator_3_gt));  // open: eq, lt
  Comparator #(.width(4), .mode("unsigned")) comparator_4 (
    .a(multiplexer_5_out), .b(4'b0011), .gt(comparator_4_gt));  // open: eq, lt
  Comparator #(.width(4), .mode("unsigned")) comparator_5 (
    .a(multiplexer_5_out), .b(4'b0010), .gt(comparator_5_gt));  // open: eq, lt
  Comparator #(.width(4), .mode("unsigned")) comparator_6 (
    .a(multiplexer_5_out), .b(4'b0000), .eq(comparator_6_eq));  // open: gt, lt
  not not_21 (not_21_out, comparator_6_eq);
  assign controlled_buffer_7_out = _4 ? comparator_3_gt : 1'bz;  // Controlled_Buffer controlled_buffer_7
  assign controlled_buffer_7_out = _3 ? comparator_4_gt : 1'bz;  // Controlled_Buffer controlled_buffer_8
  assign controlled_buffer_7_out = _2 ? comparator_5_gt : 1'bz;  // Controlled_Buffer controlled_buffer_9
  assign controlled_buffer_7_out = _0 ? not_21_out : 1'bz;  // Controlled_Buffer controlled_buffer_10

  assign K1 = 1'b1;

  // Notes on the sheet:
  //   Active el interruptor
  //   correspondiente al nivel
  //   en que desea jugar.
  //   Controlador de Frecuencia
  //   para detenerlo.
  //   MEF para el nivel del jugador
  //   Conteo
  //   Presione el botón para inicar
  //   el conteo y nuevamente
  //   MEF para estado del juego
  //   Nivel Actual
  //   Counter Asincrónico
  //   Convertidor BCD
  //   y siete
  //   Subcircuito que calcula valor absoluto de
  //   la diferencia entre número de counter
  //   Subcircuito que determina cambio de nivel en el juego
endmodule
